# Fritzing sketch circuit (saved by Fritzing 0.9.6b)

parts:
  J1 = Basic Servo
  J2 = Basic Servo
  Bauteil1 = Arduino Nano (Rev3.0) (ICSP)
  S1 = Taiway 100-SP-X-T1 SPDT Miniature Toggle Switch [part_number=100-SP-X-T1-0-0-B1-M2 package=THT]  # not connected
  U1 = SWITCH_SPDT [package=kps-1290]
  C2 = Electrolytic Capacitor [capacitance=100µF voltage=35V package="200 mil [THT, electrolytic]"]
  VCC1 = Battery
  VCC2 = Battery

nets:
  N1: J1.gnd, Bauteil1.A7
  N2: J2.gnd, Bauteil1.RESET
  N3: Bauteil1.AREF, U1.S
  N4: C2.-, VCC1.-
  N5: C2.+, VCC2.+
