# Fritzing sketch useless-box (saved by Fritzing 0.9.6b)
perfboards: 1

parts:
  Bauteil1 = Arduino Nano (Rev3.0)
  S1 = Taiway 100-SP-X-T1 SPDT Miniature Toggle Switch [part_number=100-SP-X-T1-0-0-B1-M1 package=THT]
  VCC1 = Battery
  VCC2 = Battery
  S2 = Toggle Switch [package=THT]
  C1 = Electrolytic Capacitor [capacitance=1µF voltage=35V package="100 mil [THT, electrolytic]"]
  M2 = Dagu DGServo 9g (Top view) [part_number=RS001B]
  M1 = Dagu DGServo 9g (Top view) [part_number=RS001B]

nets:
  GND: Bauteil1.GND, S1.L1, VCC1.-, C1.+, M2.gnd, M1.gnd
  N1: Bauteil1.D3, S1.L2
  N2: Bauteil1.D6, M1.pulse
  N3: Bauteil1.D9, M2.pulse
  VCC: Bauteil1.VIN, S2.L2, C1.-, M2.vcc, M1.vcc
  N4: VCC1.+, VCC2.-
  N5: VCC2.+, S2.COM

notes:
  Servos
  On/Off
  Arduino Nano
  Lever
  Batteries
